# Fritzing sketch led (saved by Fritzing 0.9.2b)
breadboards: 1

parts:
  U1 = NodeMCU V1.0
  LED1 = LED - 5mm [color="Blue (505nm)" package="5 mm [THT]"]

nets:
  N1: U1.3V3, LED1.anode
  N2: U1.GND, LED1.cathode

custom parts:
  NodeMCU V1.0: ESP8266 based NodeMCU
