# Fritzing sketch motors (saved by Fritzing 0.9.2b)
breadboards: 1

parts:
  IC1 = IC, DIP package, 16 pins [chip_label=L293D]
  U1 = NodeMCU V1.0
  M1 = DC Motor
  M2 = DC Motor
  VCC1 = 4 x AAA Battery Mount

nets:
  N1: IC1.pin1, U1.D3
  N2: IC1.pin2, U1.D1
  N3: IC1.pin3, M2.pin_2
  N4: IC1.pin4, IC1.pin13, U1.GND, VCC1.-
  N5: IC1.pin6, M2.pin_1
  N6: IC1.pin7, U1.D2
  N7: IC1.pin8, VCC1.+
  N8: IC1.pin9, U1.D6
  N9: IC1.pin10, U1.D7
  N10: IC1.pin11, M1.pin_2
  N11: IC1.pin14, M1.pin_1
  N12: IC1.pin15, U1.D8
  N13: IC1.pin16, U1.Vin

custom parts:
  NodeMCU V1.0: ESP8266 based NodeMCU
