# Fritzing sketch led (saved by Fritzing 0.9.2b)
circuit board: 8.46667cm x 5.64444cm
breadboards: 1

parts:
  LED1 = LED - 5mm [color="Red (633nm)" package="5 mm [THT]"]
  R1 = Resistor [tolerance=±5% resistance=47 package=THT]
  U1 = NodeMCU V1.0

nets:
  N1: LED1.cathode, R1.Pin_0
  N2: LED1.anode, U1.3V3
  N3: R1.Pin_1, U1.GND

notes:
  3v3
  GND

custom parts:
  NodeMCU V1.0: ESP8266 based NodeMCU
